# Fritzing sketch Scematic (saved by Fritzing 0.9.3b)
breadboards: 1

parts:
  PIR1 = PIR sensor
  PIR2 = PIR sensor
  Part1 = SRF05 Ultrasonic Rangefinder
  J1 = Piezo Speaker
  U2 = LuaNode32 / ESP32
  Squix1 = OLED 0.96" 128x64 I2C SSD1306

nets:
  VDD: PIR1.VDD, PIR2.VDD, Part1.VCC, U2.3V3, Squix1.VCC
  N1: PIR1.SIG, U2.D2
  GND: PIR1.GND, PIR2.GND, Part1.GND, J1.pin1, U2.GND, Squix1.GND
  N2: PIR2.SIG, U2.D4
  N3: Part1.Trig, U2.D19
  N4: Part1.Echo, U2.D18
  N5: J1.pin2, U2.D5
  N6: U2.D21, Squix1.SCA
  N7: U2.D22, Squix1.SCL

custom parts:
  LuaNode32 / ESP32: ESP32 based LuaNode32
